# Fritzing sketch dbg_templogger (saved by Fritzing 0.9.4)
circuit board: 8.46667cm x 5.64444cm
breadboards: 1

parts:
  Part1 = Adafruit ESP32-S2 TFT Feather [part_number="Adafruit #5300"]
  IC1 = MCP6002 [part_number=MCP6002 package=dip08]
  U1 = LIPO-1000mAh [package=lipo-1000]
  C1 = Ceramic Capacitor [capacitance=100nF package="100 mil [THT, multilayer]"]
  C2 = Ceramic Capacitor [capacitance=10µF package="100 mil [THT, multilayer]"]
  R1 = Temperature Sensor (Thermistor) [thermistor_type=NTC package=THT]
  R2 = Resistor [tolerance=±5% resistance=5.3k package="2512 [SMD]"]
  R3 = Resistor [tolerance=±5% resistance=4.7k package="0402 [SMD]"]
  R4 = Resistor [tolerance=±5% resistance=2.2k package="0402 [SMD]"]
  R5 = Resistor [tolerance=±5% resistance=10k package="0603 [SMD]"]
  R6 = Resistor [tolerance=±5% resistance=10k package="0603 [SMD]"]
  R7 = Resistor [tolerance=±5% resistance=1k package="0603 [SMD]"]
  R8 = Resistor [tolerance=±5% resistance=10k package="0603 [SMD]"]
  Part2 = Adafruit Adalogger FeatherWing [part_number="Adafruit #2922"]

nets:
  N1: Part1.SDA, Part2.SDA
  N2: Part1.SCL, Part2.SCL
  N3: Part1.TXD0, Part2.G
  N4: Part1.TX, Part2.TX
  N5: Part1.RX, Part2.RX
  N6: Part1.MISO, Part2.MISO
  N7: Part1.MOSI, Part2.MOSI
  N8: Part1.SCK, Part2.SCK
  N9: Part1.A5, Part2.F
  N10: Part1.A4, Part2.E
  N11: Part1.A3, Part2.D
  N12: Part1.A2, Part2.C
  N13: Part1.A1, Part2.B
  N14: Part1.A0, IC1.B_OUT, R8.Pin_1, Part2.A
  GND: Part1.GND, IC1.A_V-, U1.-, C1.1, C2.1, R1.pin_1, R5.Pin_0, Part2.GND
  3.3V: Part1.3.3V, IC1.A_V+, C1.0, C2.0, R2.Pin_1, R4.Pin_1, Part2.AREF, Part2.+3V3
  N15: Part1.RESET, Part2.RESET
  N16: Part1.VBAT, U1.+, Part2.VBAT
  N17: Part1.EN, Part2.EN
  N18: Part1.VBUS, Part2.USB
  N19: Part1.D13, Part2.N
  N20: Part1.D12, Part2.M
  N21: Part1.D11, Part2.L
  N22: Part1.D10, Part2.CS
  N23: Part1.D9, Part2.J
  N24: Part1.D6, Part2.I
  N25: Part1.D5, Part2.H
  N26: IC1.A_OUT, IC1.A_-IN, R6.Pin_1
  N27: IC1.A_+IN, R1.pin_0, R3.Pin_0
  N28: IC1.B_+IN, R4.Pin_0, R5.Pin_1
  N29: IC1.B_-IN, R6.Pin_0, R7.Pin_1
  N30: R2.Pin_0, R3.Pin_1
  N31: R7.Pin_0, R8.Pin_0

custom parts:
  Adafruit ESP32-S2 TFT Feather: We've got a new machine here at Adafruit, it can uncover your deepest desires. Don't believe me? I'll turn it on right now to prove it to you! What, you want unlimited mozzarella sticks? OK well, that's not something we can provide. But we can provide your second-deepest desire: an ESP32-S2 Feather board with a built in IPS TFT color display. It's got all the gooeyness of a mozzarella stick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
  MCP6002: Generic op-amp footprint
  Adafruit Adalogger FeatherWing: This is the Adalogger FeatherWing: it adds both a battery-backed Real Time Clock and micro SD card storage to any Feather main board. This FeatherWing will make it real easy to add datalogging to any of our existing Feathers. You get both an I2C real time clock (PCF8523) with 32KHz crystal and battery backup, and a microSD socket that connects to the SPI port pins (+ extra pin for CS). Tested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
